// Logisim project main.circ as structural Verilog: 2 circuits, main circuit main
module main (
);

  wire button_1_out, button_2_out, button_3_out, CLK, controle_1_down, controle_1_up, Cor_p2, Escrita, Reset,
       resetCon;
  wire [4:0] Y;
  wire [5:0] X;
  wire [23:0] Cor;

  Clock clock_1 (.out(CLK));
  Button button_1 (.out(button_1_out));
  // Rv32im #(.SocBusSelection('h0000019131E813675037061b), .stateVisible("false")) rv32im_1: pin names not known
  // RGB_Video #(.height(32), .scale(8), .width(64)) rgb_video_1: pin names not known; wires that end beside it: Reset, CLK, Escrita, X, Y, Cor
  Button button_2 (.out(button_2_out));
  Button button_3 (.out(button_3_out));
  controle controle_1 (
    .Reset(resetCon), .in_2(button_2_out), .in_3(button_3_out), .CLK(CLK), .UP(controle_1_up),
    .DOWN(controle_1_down));
  // SocPio #(.SocBusSelection('h0000019131E813675037061b), .StartAddress('h400), .direction("outputonly"), .width(6)) Saida_x: pin names not known
  // SocPio #(.SocBusSelection('h0000019131E813675037061b), .StartAddress('h418), .direction("outputonly"), .width(5)) Saida_y: pin names not known
  // SocPio #(.SocBusSelection('h0000019131E813675037061b), .StartAddress('h878), .direction("inout"), .width(2)) Controle1: pin names not known; wires that end beside it: resetCon
  // SocBus #(.SocBusIdentifier('h0000019131E813675037061b), .TraceVisible("false")) socbus_1: pin names not known
  // Socmem #(.SocBusSelection('h0000019131E813675037061b)) socmem_1: pin names not known
  // Socmem #(.SocBusSelection('h0000019131E813675037061b), .StartAddress('h478)) Memoria_de_video: pin names not known
  // SocPio #(.SocBusSelection('h0000019131E813675037061b), .StartAddress('h430), .direction("outputonly")) Reset: pin names not known
  // SocPio #(.SocBusSelection('h0000019131E813675037061b), .StartAddress('h448), .direction("outputonly")) Escrita: pin names not known; wires that end beside it: resetCon, Reset, Escrita
  // SocPio #(.SocBusSelection('h0000019131E813675037061b), .StartAddress('h460), .direction("outputonly"), .width(24)) Cor: pin names not known; wires that end beside it: Reset, Cor_p2
  D_Flip_Flop d_ff_1 (.D(Cor_p2), .clk(CLK), .Q(Escrita));  // open: Qn, preset, reset
endmodule

module controle (
  input  Reset,
  input  in_2,
  input  in_3,
  input  CLK,
  output UP,
  output DOWN
);

  wire or_1_out, or_2_out;

  D_Flip_Flop d_ff_1 (.clk(CLK), .Q(UP), .preset(in_2), .reset(or_1_out));  // open: D, Qn
  or or_1 (or_1_out, in_3, Reset);
  D_Flip_Flop d_ff_2 (.clk(CLK), .Q(DOWN), .preset(in_3), .reset(or_2_out));  // open: D, Qn
  or or_2 (or_2_out, in_2, Reset);
endmodule
